// Logisim project bp1079.circ as structural Verilog: 1 circuit, main circuit BistekProcessing1079
module BistekProcessing1079 (
  input  [7:0] Opcode,
  input  [7:0] Operand1,
  input  Clock,
  input  [7:0] Returned,
  output [7:0] ProgramCounter,
  output SetProgramCounter,
  output [7:0] DataIndex,
  output StoreSignal,
  output LoadSignal,
  output ClockSignal,
  output [7:0] Data
);

  wire ADD, and_1_out, and_3_out, and_4_out, and_5_out, and_6_out, and_8_out, ANDbw, comparator_1_eq,
       demultiplexer_1_out0, demultiplexer_1_out1, demultiplexer_1_out2, demultiplexer_1_out3, DEST, DSBX,
       JMP, JZ, MOV, MRR, NOTbw, or_2_out, or_3_out, or_6_out, or_7_out, or_8_out, ORbw, SUB, SWP, WRITERES,
       XORbw;
  wire [1:0] bit_extender_1_out;
  wire [2:0] bit_extender_2_out;
  wire [7:0] AX, BX, BXadd, BXand, BXnot, BXor, BXsub, BXxor, CX, multiplexer_2_out, multiplexer_4_out,
       multiplexer_5_out, multiplexer_6_out, multiplexer_7_out, multiplexer_8_out, multiplexer_9_out,
       multiplexer_10_out, MXDRES, ORM, RR, s833_1_carryincrement, s833_1_carryselect, s833_1_carryvalue,
       s833_2_carryincrement, s833_2_carryselect, s833_2_carryvalue, s833_3_carryincrement,
       s833_3_carryselect, s833_3_carryvalue, s833_4_carryincrement, s833_4_carryselect, s833_4_carryvalue,
       s833_5_carryincrement, s833_5_carryselect, s833_5_carryvalue;

  Bit_Extender #(.out_width(2), .\type ("zero")) bit_extender_1 (.in(Operand1), .out(bit_extender_1_out));
  Multiplexer #(.select(2), .width(8)) multiplexer_1 (
    .in0(AX), .in1(BX), .in2(CX), .in3(RR), .out(Data), .sel(bit_extender_1_out));
  S833 s833_1 (
    .SelectByte(Opcode), .IncrementValue(8'h1), .CarrySelect(s833_1_carryselect),
    .CarryValue(s833_1_carryvalue), .CarryIncrement(s833_1_carryincrement), .out_4(MOV), .out_5(DEST),
    .out_6(StoreSignal));  // open: StartingValue
  S833 s833_2 (
    .SelectByte(s833_1_carryselect), .StartingValue(s833_1_carryvalue),
    .IncrementValue(s833_1_carryincrement), .CarrySelect(s833_2_carryselect), .CarryValue(s833_2_carryvalue),
    .CarryIncrement(s833_2_carryincrement), .out_4(LoadSignal), .out_5(MRR), .out_6(JZ));
  S833 s833_3 (
    .SelectByte(s833_2_carryselect), .StartingValue(s833_2_carryvalue),
    .IncrementValue(s833_2_carryincrement), .CarrySelect(s833_3_carryselect), .CarryValue(s833_3_carryvalue),
    .CarryIncrement(s833_3_carryincrement), .out_4(SWP), .out_5(ADD), .out_6(SUB));
  S833 s833_4 (
    .SelectByte(s833_3_carryselect), .StartingValue(s833_3_carryvalue),
    .IncrementValue(s833_3_carryincrement), .CarrySelect(s833_4_carryselect), .CarryValue(s833_4_carryvalue),
    .CarryIncrement(s833_4_carryincrement), .out_4(ANDbw), .out_5(ORbw), .out_6(XORbw));
  S833 s833_5 (
    .SelectByte(s833_4_carryselect), .StartingValue(s833_4_carryvalue),
    .IncrementValue(s833_4_carryincrement), .CarrySelect(s833_5_carryselect), .CarryValue(s833_5_carryvalue),
    .CarryIncrement(s833_5_carryincrement), .out_4(NOTbw), .out_5(DSBX), .out_6(JMP));
  or or_1 (WRITERES, LoadSignal, ADD, SUB, ANDbw, ORbw, XORbw, NOTbw);
  or or_2 (or_2_out, MRR, SWP, MOV);
  and and_1 (and_1_out, or_2_out, Clock);
  or or_3 (or_3_out, JZ, JMP);
  Adder adder_1 (.a(BX), .b(AX), .out(BXadd));  // open: cin, cout
  Subtractor subtractor_1 (.a(BX), .b(AX), .out(BXsub));  // open: bin, bout
  assign BXand = BX & AX;  // AND_Gate and_2, 8 bits wide
  assign BXor = BX | AX;  // OR_Gate or_4, 8 bits wide
  assign BXxor = BX ^ AX;  // XOR_Gate xor_1, 8 bits wide
  assign BXnot = ~BX;  // NOT_Gate not_1, 8 bits wide
  Demultiplexer #(.select(3)) demultiplexer_1 (
    .out0(demultiplexer_1_out0), .out1(demultiplexer_1_out1), .out2(demultiplexer_1_out2),
    .out3(demultiplexer_1_out3), .in(and_1_out), .sel(bit_extender_2_out));  // open: out4, out5, out6, out7
  Bit_Extender #(.out_width(3), .\type ("zero")) bit_extender_2 (.in(DataIndex), .out(bit_extender_2_out));
  and and_3 (and_3_out, Clock, or_3_out);
  Comparator #(.mode("unsigned")) comparator_1 (.a(RR), .b({8{1'b0}}), .eq(comparator_1_eq));  // open: gt, lt
  Pull_Resistor pull_resistor_1 (.node(comparator_1_eq));
  Register u_AX (.D(ORM), .Q(AX), .clk(demultiplexer_1_out0));  // open: en, clr
  Multiplexer #(.width(8)) multiplexer_2 (.in0(Operand1), .in1(RR), .out(multiplexer_2_out), .sel(MRR));
  Multiplexer #(.width(8)) multiplexer_3 (.in0(multiplexer_2_out), .in1(Data), .out(ORM), .sel(SWP));
  and and_4 (and_4_out, and_3_out, comparator_1_eq);
  and and_5 (and_5_out, JMP, Clock);
  Register u_BX (.D(ORM), .Q(BX), .clk(demultiplexer_1_out1));  // open: en, clr
  or or_5 (SetProgramCounter, and_4_out, and_5_out);
  Register u_CX (.D(ORM), .Q(CX), .clk(demultiplexer_1_out2));  // open: en, clr
  and and_6 (and_6_out, WRITERES, Clock);
  Register u_RR (.D(MXDRES), .Q(RR), .clk(or_6_out));  // open: en, clr
  or or_6 (or_6_out, and_6_out, demultiplexer_1_out3);
  or or_7 (or_7_out, StoreSignal, LoadSignal);
  and and_7 (ClockSignal, or_7_out, Clock);
  Multiplexer #(.width(8)) multiplexer_4 (.in0(ORM), .in1(Returned), .out(multiplexer_4_out), .sel(LoadSignal));
  Multiplexer #(.width(8)) multiplexer_5 (.in0(multiplexer_4_out), .in1(BXadd), .out(multiplexer_5_out), .sel(ADD));
  Multiplexer #(.width(8)) multiplexer_6 (.in0(multiplexer_5_out), .in1(BXsub), .out(multiplexer_6_out), .sel(SUB));
  or or_8 (or_8_out, DEST, DSBX);
  Multiplexer #(.width(8)) multiplexer_7 (.in0(multiplexer_6_out), .in1(BXand), .out(multiplexer_7_out), .sel(ANDbw));
  Multiplexer #(.width(8)) multiplexer_8 (.in0(multiplexer_7_out), .in1(BXor), .out(multiplexer_8_out), .sel(ORbw));
  Multiplexer #(.width(8)) multiplexer_9 (.in0(Operand1), .in1(BX), .out(multiplexer_9_out), .sel(DSBX));
  Multiplexer #(.width(8)) multiplexer_10 (.in0(multiplexer_8_out), .in1(BXxor), .out(multiplexer_10_out), .sel(XORbw));
  Multiplexer #(.width(8)) multiplexer_11 (.in0(multiplexer_10_out), .in1(BXnot), .out(MXDRES), .sel(NOTbw));
  and and_8 (and_8_out, or_8_out, Clock);
  assign ProgramCounter = SetProgramCounter ? CX : 8'bz;  // Controlled_Buffer controlled_buffer_1
  Register DI (.D(multiplexer_9_out), .Q(DataIndex), .clk(and_8_out));  // open: en, clr

  // Other names for the same wires on the sheet: DI[7:0] = DataIndex; LD = LoadSignal; LDR[7:0] = Returned;
  //   MXDREG[7:0] = Data; Op1[7:0] = Operand1; SPC = SetProgramCounter; STR = StoreSignal

  // Notes on the sheet:
  //   Inputs
  //   Decoder
  //   GPRs - Accumulate, Base, Counter, Result
  //   idk random stuff
  //   RAM
  //   DI - Destination Index
endmodule
