// Logisim project bp1080.circ as structural Verilog: 1 circuit, main circuit BistekProcessing1080
module BistekProcessing1080 (
  input  [7:0] Opcode,
  input  [15:0] Operand1,
  input  Clock,
  input  [15:0] EXTRAMRD,
  input  [15:0] ProgramCounterIn,
  output [15:0] ProgramCounter,
  output SetProgramCounter,
  output [15:0] EXTRAMADR,
  output EXTRAMWE,
  output EXTRAMOE,
  output EXTRAMCL,
  output [15:0] EXTRAMDAT
);

  wire ADD, and_1_out, and_3_out, and_4_out, and_6_out, and_7_out, ANDbw, CMP, comparator_1_eq,
       demultiplexer_1_out0, demultiplexer_1_out1, demultiplexer_1_out2, demultiplexer_1_out3, DEST, DSBX,
       JMP, JMPI, JZ, JZI, LOGOP, MOV, MRR, NOTbw, or_2_out, or_4_out, or_5_out, or_8_out, or_9_out, ORbw,
       PCCX, RESULTS, RRZ, SETDEST, SUB, SWP, WRITE, XORbw;
  wire [1:0] bit_extender_1_out, bit_extender_2_out;
  wire [7:0] s833_1_carryincrement, s833_1_carryselect, s833_1_carryvalue, s833_2_carryincrement,
       s833_2_carryselect, s833_2_carryvalue, s833_3_carryincrement, s833_3_carryselect, s833_3_carryvalue,
       s833_4_carryincrement, s833_4_carryselect, s833_4_carryvalue, s833_5_carryincrement,
       s833_5_carryselect, s833_5_carryvalue, s833_6_carryincrement, s833_6_carryselect, s833_6_carryvalue;
  wire [15:0] AX, BX, BXADD, BXAND, BXCMP, BXNOT, BXOR, BXSUB, BXXOR, CX, DESTDATA, DESTINATION, LOGOPRES,
       multiplexer_1_out, multiplexer_2_out, multiplexer_5_out, multiplexer_6_out, multiplexer_7_out,
       multiplexer_8_out, multiplexer_9_out, multiplexer_10_out, multiplexer_11_out, multiplexer_12_out,
       multiplexer_13_out, multiplexer_17_out, multiplexer_19_out, RES, RR, WRITEDATA;

  Multiplexer #(.width(16)) multiplexer_1 (.in0(EXTRAMADR), .in1(16'h3), .out(multiplexer_1_out), .sel(RESULTS));
  Multiplexer #(.width(16)) multiplexer_2 (.in0(multiplexer_1_out), .in1(Operand1), .out(multiplexer_2_out), .sel(MRR));
  Multiplexer #(.width(16)) multiplexer_3 (.in0(multiplexer_2_out), .in1(16'h2), .out(DESTINATION), .sel(PCCX));
  Bit_Extender #(.in_width(16), .out_width(2), .\type ("zero")) bit_extender_1 (
    .in(Operand1), .out(bit_extender_1_out));
  Multiplexer #(.select(2), .width(16)) multiplexer_4 (
    .in0(AX), .in1(BX), .in2(CX), .in3(RR), .out(EXTRAMDAT), .sel(bit_extender_1_out));
  and and_1 (and_1_out, Clock, WRITE);
  Demultiplexer #(.select(2)) demultiplexer_1 (
    .out0(demultiplexer_1_out0), .out1(demultiplexer_1_out1), .out2(demultiplexer_1_out2),
    .out3(demultiplexer_1_out3), .in(and_1_out), .sel(bit_extender_2_out));
  Bit_Extender #(.in_width(16), .out_width(2), .\type ("zero")) bit_extender_2 (
    .in(DESTINATION), .out(bit_extender_2_out));
  Multiplexer #(.width(16)) multiplexer_5 (.in0(BXADD), .in1(BXSUB), .out(multiplexer_5_out), .sel(SUB));
  Adder #(.width(16)) adder_1 (.a(BX), .b(AX), .out(BXADD));  // open: cin, cout
  Subtractor #(.width(16)) subtractor_1 (.a(BX), .b(AX), .out(BXSUB));  // open: bin, bout
  assign BXAND = BX & AX;  // AND_Gate and_2, 16 bits wide
  assign BXOR = BX | AX;  // OR_Gate or_1, 16 bits wide
  assign BXXOR = BX ^ AX;  // XOR_Gate xor_1, 16 bits wide
  assign BXNOT = ~BX;  // NOT_Gate not_1, 16 bits wide
  Comparator #(.mode("unsigned"), .width(16)) comparator_1 (.a(BX), .b(AX), .eq(comparator_1_eq));  // open: gt, lt
  Multiplexer #(.width(16)) multiplexer_6 (.in0(multiplexer_5_out), .in1(BXAND), .out(multiplexer_6_out), .sel(ANDbw));
  Multiplexer #(.width(16)) multiplexer_7 (.in0(multiplexer_6_out), .in1(BXOR), .out(multiplexer_7_out), .sel(ORbw));
  assign BXCMP = {{15{1'b0}}, comparator_1_eq};  // Bit_Extender bit_extender_3
  Register #(.width(16)) u_AX (.D(WRITEDATA), .Q(AX), .clk(demultiplexer_1_out0));  // open: en, clr
  Multiplexer #(.width(16)) multiplexer_8 (.in0(Operand1), .in1(EXTRAMDAT), .out(multiplexer_8_out), .sel(SWP));
  Multiplexer #(.width(16)) multiplexer_9 (.in0(multiplexer_8_out), .in1(RES), .out(multiplexer_9_out), .sel(RESULTS));
  Multiplexer #(.width(16)) multiplexer_10 (
    .in0(multiplexer_7_out), .in1(BXXOR), .out(multiplexer_10_out), .sel(XORbw));
  Multiplexer #(.width(16)) multiplexer_11 (
    .in0(multiplexer_10_out), .in1(BXNOT), .out(multiplexer_11_out), .sel(NOTbw));
  Multiplexer #(.width(16)) multiplexer_12 (.in0(multiplexer_11_out), .in1(BXCMP), .out(multiplexer_12_out), .sel(CMP));
  Register #(.width(16)) u_BX (.D(WRITEDATA), .Q(BX), .clk(demultiplexer_1_out1));  // open: en, clr
  or or_2 (or_2_out, demultiplexer_1_out3, and_3_out);
  and and_3 (and_3_out, RESULTS, Clock);
  or or_3 (SETDEST, DEST, DSBX);
  Multiplexer #(.width(16)) multiplexer_13 (.in0(multiplexer_9_out), .in1(RR), .out(multiplexer_13_out), .sel(MRR));
  Multiplexer #(.width(16)) multiplexer_14 (
    .in0(multiplexer_13_out), .in1(ProgramCounterIn), .out(WRITEDATA), .sel(PCCX));
  Multiplexer #(.width(16)) multiplexer_15 (.in0({16{1'b0}}), .in1(multiplexer_12_out), .out(LOGOPRES), .sel(LOGOP));
  Register #(.width(16)) u_CX (.D(WRITEDATA), .Q(CX), .clk(demultiplexer_1_out2));  // open: en, clr
  Register #(.width(16)) u_RR (.D(WRITEDATA), .Q(RR), .clk(or_2_out));  // open: en, clr
  Register #(.width(16)) DI (.D(DESTDATA), .Q(EXTRAMADR), .clk(and_4_out));  // open: en, clr
  and and_4 (and_4_out, SETDEST, Clock);
  or or_4 (or_4_out, JMPI, JZI);
  Pull_Resistor pull_resistor_1 (.node(RRZ));
  Comparator #(.mode("unsigned"), .width(16)) comparator_2 (.a(RR), .b({16{1'b0}}), .eq(RRZ));  // open: gt, lt
  Multiplexer #(.width(16)) multiplexer_16 (.in0(Operand1), .in1(BX), .out(DESTDATA), .sel(DSBX));
  Multiplexer #(.width(16)) multiplexer_17 (.in0(CX), .in1(Operand1), .out(multiplexer_17_out), .sel(or_4_out));
  Multiplexer #(.width(16)) multiplexer_18 (
    .in0({16{1'b0}}), .in1(multiplexer_17_out), .out(ProgramCounter), .sel(SetProgramCounter));
  Pull_Resistor pull_resistor_2 (.node(ProgramCounter));
  or or_5 (or_5_out, EXTRAMOE, EXTRAMWE);
  and and_5 (EXTRAMCL, or_5_out, Clock);
  or or_6 (RESULTS, EXTRAMOE, LOGOP);
  or or_7 (LOGOP, ADD, SUB, ANDbw, CMP, ORbw, XORbw, NOTbw);
  or or_8 (or_8_out, JZ, JZI);
  or or_9 (or_9_out, JMP, JMPI);
  Multiplexer #(.width(16)) multiplexer_19 (.in0(EXTRAMRD), .in1(LOGOPRES), .out(multiplexer_19_out), .sel(LOGOP));
  Multiplexer #(.width(16)) multiplexer_20 (.in0({16{1'b0}}), .in1(multiplexer_19_out), .out(RES), .sel(RESULTS));
  and and_6 (and_6_out, or_8_out, Clock, RRZ);
  and and_7 (and_7_out, or_9_out, Clock);
  or or_10 (WRITE, MOV, SWP, PCCX, MRR);
  or or_11 (SetProgramCounter, and_6_out, and_7_out);
  S833 s833_1 (
    .SelectByte(Opcode), .IncrementValue(8'h1), .CarrySelect(s833_1_carryselect),
    .CarryValue(s833_1_carryvalue), .CarryIncrement(s833_1_carryincrement), .out_4(MOV), .out_5(DEST),
    .out_6(EXTRAMWE));  // open: StartingValue
  S833 s833_2 (
    .SelectByte(s833_1_carryselect), .StartingValue(s833_1_carryvalue),
    .IncrementValue(s833_1_carryincrement), .CarrySelect(s833_2_carryselect), .CarryValue(s833_2_carryvalue),
    .CarryIncrement(s833_2_carryincrement), .out_4(EXTRAMOE), .out_5(MRR), .out_6(JZ));
  S833 s833_3 (
    .SelectByte(s833_2_carryselect), .StartingValue(s833_2_carryvalue),
    .IncrementValue(s833_2_carryincrement), .CarrySelect(s833_3_carryselect), .CarryValue(s833_3_carryvalue),
    .CarryIncrement(s833_3_carryincrement), .out_4(SWP), .out_5(ADD), .out_6(SUB));
  S833 s833_4 (
    .SelectByte(s833_3_carryselect), .StartingValue(s833_3_carryvalue),
    .IncrementValue(s833_3_carryincrement), .CarrySelect(s833_4_carryselect), .CarryValue(s833_4_carryvalue),
    .CarryIncrement(s833_4_carryincrement), .out_4(ANDbw), .out_5(ORbw), .out_6(XORbw));
  S833 s833_5 (
    .SelectByte(s833_4_carryselect), .StartingValue(s833_4_carryvalue),
    .IncrementValue(s833_4_carryincrement), .CarrySelect(s833_5_carryselect), .CarryValue(s833_5_carryvalue),
    .CarryIncrement(s833_5_carryincrement), .out_4(NOTbw), .out_5(DSBX), .out_6(JMP));
  S833 s833_6 (
    .SelectByte(s833_5_carryselect), .StartingValue(s833_5_carryvalue),
    .IncrementValue(s833_5_carryincrement), .CarrySelect(s833_6_carryselect), .CarryValue(s833_6_carryvalue),
    .CarryIncrement(s833_6_carryincrement), .out_4(PCCX), .out_5(JMPI), .out_6(JZI));
  S833 s833_7 (
    .SelectByte(s833_6_carryselect), .StartingValue(s833_6_carryvalue),
    .IncrementValue(s833_6_carryincrement), .out_4(CMP));  // open: CarrySelect, CarryValue, CarryIncrement, out_5, out_6

  // Other names for the same wires on the sheet: DI[15:0] = EXTRAMADR; LD = EXTRAMOE; LDR[15:0] = EXTRAMRD;
  //   MXD[15:0] = EXTRAMDAT; OP0[7:0] = Opcode; OP1[15:0] = Operand1; PC[15:0] = ProgramCounterIn;
  //   SPC = SetProgramCounter; STR = EXTRAMWE
endmodule
