// Logisim project kola_system_four.circ as structural Verilog: 1 circuit, main circuit main
module main (
);

  wire bistekprocessing1080_1_extramcl, bistekprocessing1080_1_extramoe, bistekprocessing1080_1_extramwe,
       bistekprocessing1080_1_setprogramcounter, clock_1_out, or_1_out, pull_resistor_1_node, s_r_ff_1_q,
       START_out, STOP_out;
  wire [15:0] bistekprocessing1080_1_extramadr, bistekprocessing1080_1_extramdat,
       bistekprocessing1080_1_programcounter, counter_1_q, ram_1_dout;
  wire [23:0] rom_1_data;

  ROM #(.addrWidth(16), .dataWidth(24)) rom_1 (.addr(counter_1_q), .data(rom_1_data));
  Clock clock_1 (.out(clock_1_out));
  Button START (.out(START_out));
  or or_1 (or_1_out, START_out, STOP_out);
  Button STOP (.out(STOP_out));
  S_R_Flip_Flop s_r_ff_1 (.S(START_out), .clk(or_1_out), .R(STOP_out), .Q(s_r_ff_1_q));  // open: Qn, preset, reset
  Pull_Resistor pull_resistor_1 (.node(pull_resistor_1_node));
  assign pull_resistor_1_node = s_r_ff_1_q ? clock_1_out : 1'bz;  // Controlled_Buffer controlled_buffer_1
  BistekProcessing1080 bistekprocessing1080_1 (
    .Opcode(rom_1_data[7:0]), .Operand1(rom_1_data[23:8]), .Clock(pull_resistor_1_node),
    .ProgramCounterIn(counter_1_q), .ProgramCounter(bistekprocessing1080_1_programcounter),
    .SetProgramCounter(bistekprocessing1080_1_setprogramcounter),
    .EXTRAMADR(bistekprocessing1080_1_extramadr), .EXTRAMWE(bistekprocessing1080_1_extramwe),
    .EXTRAMOE(bistekprocessing1080_1_extramoe), .EXTRAMCL(bistekprocessing1080_1_extramcl),
    .EXTRAMDAT(bistekprocessing1080_1_extramdat), .EXTRAMRD(ram_1_dout));
  Counter #(.max('hffff), .trigger("falling"), .width(16)) counter_1 (
    .load(bistekprocessing1080_1_setprogramcounter), .D(bistekprocessing1080_1_programcounter),
    .Q(counter_1_q), .clk(pull_resistor_1_node), .clr(STOP_out));  // open: count, carry, up
  RAM #(.addrWidth(16), .dataWidth(16)) ram_1 (
    .addr(bistekprocessing1080_1_extramadr), .we(bistekprocessing1080_1_extramwe),
    .oe(bistekprocessing1080_1_extramoe), .clk(bistekprocessing1080_1_extramcl),
    .din(bistekprocessing1080_1_extramdat), .dout(ram_1_dout));

  // Notes on the sheet:
  //   contents of rom_1 (hex, n*v repeats v):
  //   1 5500 2 101 5500 1 100 8 1 302 d11 104 710 d10
endmodule
