// Logisim project s833chip.circ as structural Verilog: 1 circuit, main circuit S833
module S833 (
  input  [7:0] SelectByte,
  input  [7:0] StartingValue,
  input  [7:0] IncrementValue,
  output out_4,
  output out_5,
  output out_6,
  output [7:0] CarrySelect,
  output [7:0] CarryValue,
  output [7:0] CarryIncrement
);

  wire [7:0] adder_1_out, adder_2_out, not_1_out, not_2_out, not_3_out, xor_1_out, xor_2_out, xor_3_out;

  Adder adder_1 (.a(StartingValue), .b(IncrementValue), .out(adder_1_out));  // open: cin, cout
  Adder adder_2 (.a(adder_1_out), .b(IncrementValue), .out(adder_2_out));  // open: cin, cout
  Adder adder_3 (.a(adder_2_out), .b(IncrementValue), .out(CarryValue));  // open: cin, cout
  assign xor_1_out = SelectByte ^ StartingValue;  // XOR_Gate xor_1, 8 bits wide
  assign not_1_out = ~xor_1_out;  // NOT_Gate not_1, 8 bits wide
  assign xor_2_out = SelectByte ^ adder_1_out;  // XOR_Gate xor_2, 8 bits wide
  assign not_2_out = ~xor_2_out;  // NOT_Gate not_2, 8 bits wide
  assign xor_3_out = SelectByte ^ adder_2_out;  // XOR_Gate xor_3, 8 bits wide
  assign not_3_out = ~xor_3_out;  // NOT_Gate not_3, 8 bits wide
  and and_1 (out_4, not_1_out[0], not_1_out[1], not_1_out[2], not_1_out[3], not_1_out[4], not_1_out[5], not_1_out[6], not_1_out[7]);
  and and_2 (out_5, not_2_out[0], not_2_out[1], not_2_out[2], not_2_out[3], not_2_out[4], not_2_out[5], not_2_out[6], not_2_out[7]);
  and and_3 (out_6, not_3_out[0], not_3_out[1], not_3_out[2], not_3_out[3], not_3_out[4], not_3_out[5], not_3_out[6], not_3_out[7]);

  assign CarryIncrement = IncrementValue;
  assign CarrySelect = SelectByte;
endmodule
